# Fritzing sketch Jetson_Orin (saved by Fritzing 0.9.3b)

parts:
  M1 = DC Motor
  J1 = Basic Servo
  PWM1 = PCA9685 16x12-bit PWM Breakout
  J2 = Basic Servo
  J3 = Basic Servo
  부품1 = Adafruit DC+Stepper Motor HAT [part_number="Adafruit #2348"]
  Jetson_Nano1 = Jetson Nano

nets (from the breadboard view):
  N1: M1.pin_1, 부품1.M1B
  N2: M1.pin_2, 부품1.M1A
  GND: J1.gnd, PWM1.no_name_yet#501, PWM1.no_name_yet#1000, PWM1.no_name_yet#1001, PWM1.no_name_yet#1002, J2.gnd, J3.gnd, 부품1.GND, Jetson_Nano1.GPIO13, Jetson_Nano1.GPIO19
  VCC: J1.vcc, PWM1.no_name_yet#100, PWM1.no_name_yet#101, PWM1.no_name_yet#102, PWM1.no_name_yet#506, J2.vcc, J3.vcc, Jetson_Nano1.GPIO26
  N3: J1.pulse, PWM1.no_name_yet#2
  N4: PWM1.no_name_yet#0, J3.pulse
  N5: PWM1.no_name_yet#1, J2.pulse
  N6: PWM1.no_name_yet#503, PWM1.no_name_yet#505, 부품1.5.0V, Jetson_Nano1.GND, Jetson_Nano1.GPIO16
  N7: PWM1.no_name_yet#504, Jetson_Nano1.GPIO20
  N8: Jetson_Nano1.GPIO5, Jetson_Nano1.GPIO6

notes:
  Raspberry Pi 5
  USB Mic
  Lidar

custom parts:
  Adafruit DC+Stepper Motor HAT: Let your robotic dreams come true with the new DC+Stepper Motor HAT from Adafruit. This Raspberry Pi add-on is perfect for any motion project as it can drive up to 4 DC or 2 Stepper motors with full PWM speed control. Since the Raspberry Pi does not have a lot of PWM pins, we use a fully-dedicated PWM driver chip onboard to both control motor direction and speed. This chip handles all the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
