# Fritzing sketch ssafy_pjt (saved by Fritzing 0.9.3b)
breadboards: 1

parts:
  A1 = Raspberry Pi 5
  VALVE1 = Plastic Solenoid Valve
  IC1 = Rasberry Pi NIOR Camera [chip_label=IC package="DIP (Dual Inline) [THT]"]  # not connected
  IC2 = Rasberry Pi NIOR Camera [chip_label=IC package="DIP (Dual Inline) [THT]"]  # not connected
  IC3 = Rasberry Pi NIOR Camera [chip_label=IC package="DIP (Dual Inline) [THT]"]  # not connected
  DC-DC_5V-12V = LM2596 step down module
  IC4 = Rasberry Pi NIOR Camera [chip_label=IC package="DIP (Dual Inline) [THT]"]  # not connected
  IC5 = Rasberry Pi NIOR Camera [chip_label=IC package="DIP (Dual Inline) [THT]"]  # not connected
  IC6 = Rasberry Pi NIOR Camera [chip_label=IC package="DIP (Dual Inline) [THT]"]  # not connected
  M1 = gy9250
  KF-1 = KF-301 Relay [package=THT]
  VCC1 = 4 x AAA Battery Mount
  VCC2 = 4 x AAA Battery Mount

nets (from the schematic view):
  N1: A1.3V3, M1.pin1
  N2: A1.GPIO2, M1.pin4
  N3: A1.GPIO3, M1.pin3
  N4: A1.GND, M1.pin2, KF-1.ground, VCC1.-
  N5: A1.GPIO25, KF-1.signal
  N6: VALVE1.no_name_yet#1, KF-1.NC
  N7: VALVE1.no_name_yet#2, DC-DC_5V-12V.IN-, DC-DC_5V-12V.OUT-, VCC2.-
  N8: DC-DC_5V-12V.IN+, VCC2.+
  N9: DC-DC_5V-12V.OUT+, KF-1.C
  N10: KF-1.power, VCC1.+

notes:
  DC 5V
  DC 12V
  Solenoid Actuator
  총알 발사
  PI 5
  MPU9250
  방향 측정
  Relay
  발사 제어
  PI Camera

custom parts:
  Raspberry Pi 5: The RPi5, a faster version of the awesome Raspberry Pi4B ARM Board with 40 pin gpio.
  Rasberry Pi NIOR Camera: Camera
  LM2596 step down module: LM2596 DC-DC step down power supply module 3 A.
  gy9250: MPU-9250 module (three-axis gyroscope + three-axis acceleration + three-axis magnetic field). The generic model from ebay et. al. rather than the Sparkfun version.
  KF-301 Relay: KF-301
